// Logisim project Ctl_Opcode_Decoder.circ as structural Verilog: 1 circuit, main circuit Opcode_Decoder
module Opcode_Decoder (
  input  [5:0] Opcode,
  output Shift,
  output Data_Processing,
  output Load_Store,
  output SP_Address,
  output Conditional
);

  wire not_1_out, not_2_out, not_3_out, not_4_out, not_5_out;

  not not_1 (not_1_out, Opcode[0]);
  not not_2 (not_2_out, Opcode[1]);
  not not_3 (not_3_out, Opcode[1]);
  not not_4 (not_4_out, Opcode[2]);
  Comparator #(.width(6)) comparator_1 (.a(Opcode), .b(6'b101100), .eq(SP_Address));  // open: gt, lt
  not not_5 (not_5_out, Opcode[2]);
  and and_1 (Shift, not_1_out, not_2_out);
  Comparator #(.width(6)) comparator_2 (.a(Opcode), .b(6'b010000), .eq(Data_Processing));  // open: gt, lt
  and and_2 (Load_Store, Opcode[0], not_3_out, not_4_out, Opcode[3]);
  and and_3 (Conditional, Opcode[0], Opcode[1], not_5_out, Opcode[3]);

  // Other names for the same wires on the sheet: b5 = Opcode[0]; b4 = Opcode[1]; b3 = Opcode[2]; b2 = Opcode[3];
  //   b1 = Opcode[4]; b0 = Opcode[5]

  // Notes on the sheet:
  //   Shift, add, sub, mov
  //   Data Processing
  //   Load/Store
  //   SP Address
  //   Conditional branch
endmodule
